# Fritzing sketch LedMatrix-595 (saved by Fritzing 0.9.3b)
breadboards: 2

parts:
  R4 = Resistor [tolerance=±5% resistance=330 package=THT]
  R5 = Resistor [tolerance=±5% resistance=330 package=THT]
  R6 = Resistor [tolerance=±5% resistance=330 package=THT]
  R7 = Resistor [tolerance=±5% resistance=330 package=THT]
  R8 = Resistor [tolerance=±5% resistance=330 package=THT]
  Disp1 = LBT2088AH [part_number=LBT2088AH]
  R11 = Resistor [tolerance=±5% resistance=330 package=THT]
  U1 = 74HC595 [package="DIP16 [THT]"]
  Part1 = Arduino Uno (Rev3)
  R12 = Resistor [tolerance=±5% resistance=330 package=THT]
  R13 = Resistor [tolerance=±5% resistance=330 package=THT]

nets:
  N1: R4.Pin_0, Disp1.pin_4
  N2: R4.Pin_1, Part1.D4
  N3: R5.Pin_0, Disp1.pin_10
  N4: R5.Pin_1, Part1.D5_PWM
  N5: R6.Pin_0, Disp1.pin_6
  N6: R6.Pin_1, Part1.D6_PWM
  N7: R7.Pin_0, Disp1.pin_11
  N8: R7.Pin_1, Part1.D7
  N9: R8.Pin_0, Disp1.pin_15
  N10: R8.Pin_1, Part1.D8
  N11: Disp1.pin1, U1.Q4
  N12: Disp1.pin2, U1.Q6
  N13: Disp1.pin_3, R12.Pin_0
  N14: Disp1.pin_5, U1.Q7
  N15: Disp1.pin_7, U1.Q5
  N16: Disp1.pin_8, U1.Q2
  N17: Disp1.pin_9, U1.Q0
  N18: Disp1.pin_12, U1.Q3
  N19: Disp1.pin_13, R13.Pin_0
  N20: Disp1.pin_14, U1.Q1
  N21: Disp1.pin_16, R11.Pin_0
  N22: R11.Pin_1, Part1.D9_PWM
  GND: U1.GND, U1.OE, Part1.GND
  VCC: U1.MR, U1.VCC, Part1.5V
  N23: U1.SH_CP, Part1.D12/MISO
  N24: U1.ST_CP, Part1.D11_PWM/MOSI
  N25: U1.DS, Part1.D10_PWM/SS
  N26: Part1.D2, R13.Pin_1
  N27: Part1.D3_PWM, R12.Pin_1
